# Fritzing sketch wiring (saved by Fritzing 0.9.3b)
breadboards: 1

parts:
  Teensy1 = Teensy 2.0
  Part1 = Adafruit MCP4725 Breakout Board - 12-Bit DAC [part_number="Adafruit #935"]

nets (from the schematic view):
  GND: Teensy1.GND, Part1.GND
  N1: Teensy1.D0, Part1.SCL
  N2: Teensy1.D1, Part1.SDA
  5V: Part1.VDD

custom parts:
  Adafruit MCP4725 Breakout Board - 12-Bit DAC: Your microcontroller probably has an ADC (analog -> digital converter) but does it have a DAC (digital -> analog converter)??? Now it can! This breakout board features the easy-to-use MCP4725 12-bit DAC. Control it via I2C and send it the value you want it to output, and the VOUT pin will have it. Great for audio / analog projects, such as when you can't use PWM but need a sine wave or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
